// Logisim project aialu.circ as structural Verilog
module Full_Adder (
  input  A,
  input  B,
  input  C,
  output out_4,
  output out_5
);

  wire and_1_out, and_2_out, xor_1_out;

  xor xor_1 (xor_1_out, A, B);
  xor xor_2 (out_4, xor_1_out, C);
  and and_1 (and_1_out, C, xor_1_out);
  and and_2 (and_2_out, B, A);
  or or_1 (out_5, and_1_out, and_2_out);
endmodule

module Half_Adder (
  input  A,
  input  B,
  output S,
  output C
);

  xor xor_1 (S, A, B);
  and and_1 (C, A, B);
endmodule

module Complemento_A2 (
  input  [7:0] A,
  input  [7:0] B,
  output out_3,
  output [7:0] out_4
);

  wire full_adder_1_out_4, full_adder_2_out_4, full_adder_3_out_4, full_adder_4_out_4, full_adder_5_out_4,
       full_adder_6_out_4, half_adder_1_c;
  wire [7:0] not_1_out;

  Half_Adder half_adder_1 (.A(A[0]), .B(not_1_out[0]), .S(out_4[7]), .C(half_adder_1_c));
  assign not_1_out = ~B;  // NOT_Gate not_1, 8 bits wide
  Full_Adder full_adder_1 (
    .A(A[1]), .B(not_1_out[1]), .C(half_adder_1_c), .out_4(full_adder_1_out_4), .out_5(out_4[6]));
  Full_Adder full_adder_2 (
    .A(A[2]), .B(not_1_out[2]), .C(full_adder_1_out_4), .out_4(full_adder_2_out_4), .out_5(out_4[5]));
  Full_Adder full_adder_3 (
    .A(A[3]), .B(not_1_out[3]), .C(full_adder_2_out_4), .out_4(full_adder_3_out_4), .out_5(out_4[4]));
  Full_Adder full_adder_4 (
    .A(A[4]), .B(not_1_out[4]), .C(full_adder_3_out_4), .out_4(full_adder_4_out_4), .out_5(out_4[3]));
  Full_Adder full_adder_5 (
    .A(A[5]), .B(not_1_out[5]), .C(full_adder_4_out_4), .out_4(full_adder_5_out_4), .out_5(out_4[2]));
  Full_Adder full_adder_6 (
    .A(A[6]), .B(not_1_out[6]), .C(full_adder_5_out_4), .out_4(full_adder_6_out_4), .out_5(out_4[1]));
  Full_Adder full_adder_7 (.A(A[7]), .B(not_1_out[7]), .C(full_adder_6_out_4), .out_4(out_3), .out_5(out_4[0]));
endmodule
