// Logisim project s1.circ as structural Verilog
module Half_Adder (
  input  A,
  input  B,
  output Somma,
  output Riporto
);

  xor xor_1 (Somma, A, B);
  and and_1 (Riporto, A, B);
endmodule

module Full_Adder (
  input  A,
  input  B,
  input  C,
  output Somma,
  output Riporto
);

  wire and_1_out, and_2_out, and_3_out, xor_1_out;

  xor xor_1 (xor_1_out, A, B);
  and and_1 (and_1_out, A, C);
  and and_2 (and_2_out, A, B);
  and and_3 (and_3_out, B, C);
  xor xor_2 (Somma, xor_1_out, C);
  or or_1 (Riporto, and_1_out, and_2_out, and_3_out);
endmodule

module sommatore_8 (
  input  [7:0] A,
  input  [7:0] B,
  input  in_3,
  output [7:0] out_4,
  output overflow
);

  wire c1, c2, c3, c4, c5, c6, c7;

  Full_Adder full_adder_1 (.Somma(out_4[0]), .Riporto(c1), .A(A[0]), .B(B[0]), .C(in_3));
  Full_Adder full_adder_2 (.Somma(out_4[7]), .Riporto(overflow), .A(A[7]), .B(B[7]), .C(c7));
  Full_Adder full_adder_3 (.Somma(out_4[6]), .Riporto(c7), .A(A[6]), .B(B[6]), .C(c6));
  Full_Adder full_adder_4 (.Somma(out_4[1]), .Riporto(c2), .A(A[1]), .B(B[1]), .C(c1));
  Full_Adder full_adder_5 (.Somma(out_4[2]), .Riporto(c3), .A(A[2]), .B(B[2]), .C(c2));
  Full_Adder full_adder_6 (.Somma(out_4[3]), .Riporto(c4), .A(A[3]), .B(B[3]), .C(c3));
  Full_Adder full_adder_7 (.Somma(out_4[4]), .Riporto(c5), .A(A[4]), .B(B[4]), .C(c4));
  Full_Adder full_adder_8 (.Somma(out_4[5]), .Riporto(c6), .A(A[5]), .B(B[5]), .C(c5));

  // Other names for the same wires on the sheet: a_t = A[1]; c = A[2]; e = A[3]; g = A[4]; i = A[5]; m = A[6];
  //   o = A[7]; b_t = B[1]; d = B[2]; f = B[3]; h = B[4]; l = B[5]; n = B[6]; p = B[7]; s1 = out_4[0]; s2 = out_4[1];
  //   s3 = out_4[2]; s4 = out_4[3]; s5 = out_4[4]; s6 = out_4[5]; s7 = out_4[6]; s8 = out_4[7]
endmodule

module sottrattore_8 (
  input  [7:0] A,
  input  [7:0] B,
  output [7:0] out_3,
  output Overflow
);

  wire and_1_out, b_t, c1, c2, c3, c4, c5, c6, c7, d, f, h, l, n, p, xnor_1_out;
  wire [0:0] not_1_out;

  // Probe on A
  // Probe on B
  Full_Adder full_adder_1 (.Somma(out_3[0]), .Riporto(c1), .A(A[0]), .B(not_1_out[0]), .C(1'b1));
  Full_Adder full_adder_2 (.Somma(out_3[7]), .A(A[7]), .B(p), .C(c7));  // open: Riporto
  xnor xnor_1 (xnor_1_out, A[7], p);
  assign {p, n, l, h, f, d, b_t, not_1_out[0]} = ~B;  // NOT_Gate not_1, 8 bits wide
  and and_1 (and_1_out, xnor_1_out, p, A[7]);
  Full_Adder full_adder_3 (.Somma(out_3[6]), .Riporto(c7), .A(A[6]), .B(n), .C(c6));
  and and_2 (Overflow, and_1_out, c7);
  Full_Adder full_adder_4 (.Somma(out_3[1]), .Riporto(c2), .A(A[1]), .B(b_t), .C(c1));
  Full_Adder full_adder_5 (.Somma(out_3[2]), .Riporto(c3), .A(A[2]), .B(d), .C(c2));
  Full_Adder full_adder_6 (.Somma(out_3[3]), .Riporto(c4), .A(A[3]), .B(f), .C(c3));
  Full_Adder full_adder_7 (.Somma(out_3[4]), .Riporto(c5), .A(A[4]), .B(h), .C(c4));
  Full_Adder full_adder_8 (.Somma(out_3[5]), .Riporto(c6), .A(A[5]), .B(l), .C(c5));
  // Probe on out_3

  // Other names for the same wires on the sheet: a_t = A[1]; c = A[2]; e = A[3]; g = A[4]; i = A[5]; m = A[6];
  //   o = A[7]; s1 = out_3[0]; s2 = out_3[1]; s3 = out_3[2]; s4 = out_3[3]; s5 = out_3[4]; s6 = out_3[5];
  //   s7 = out_3[6]; s8 = out_3[7]
endmodule

module AiArith (
  input  [7:0] A,
  input  [7:0] B,
  input  Enable,
  input  in_4,
  output [7:0] out_5,
  output out_6
);

  wire sommatore_8_1_overflow, sottrattore_8_1_overflow;
  wire [7:0] sommatore_8_1_out_4, sottrattore_8_1_out_3;

  sottrattore_8 sottrattore_8_1 (.out_3(sottrattore_8_1_out_3), .A(A), .B(B), .Overflow(sottrattore_8_1_overflow));
  sommatore_8 sommatore_8_1 (.out_4(sommatore_8_1_out_4), .overflow(sommatore_8_1_overflow), .A(A), .B(B), .in_3(in_4));
  or or_1 (out_6, sottrattore_8_1_overflow, sommatore_8_1_overflow);
  assign out_5 = sottrattore_8_1_out_3 | sommatore_8_1_out_4;  // OR_Gate or_2, 8 bits wide
endmodule

module AiArith2 (
  input  [7:0] A,
  input  in_2,
  input  [7:0] B,
  input  _0____1,
  output [7:0] out_5,
  output out_6
);

  AiArith aiarith_1 (.Enable(_0____1), .out_5(out_5), .A(A), .B(B), .in_4(in_2), .out_6(out_6));
endmodule

module Mux_8bit (
  input  S0,
  input  S1,
  input  S2,
  input  D0,
  input  D1,
  input  D2,
  input  D3,
  input  D4,
  input  D5,
  input  D6,
  input  D7,
  output out_12
);

  wire and_1_out, and_2_out, and_3_out, and_4_out, and_5_out, and_6_out, and_7_out, and_8_out, not_1_out,
       not_2_out, not_3_out;

  not not_1 (not_1_out, S0);
  not not_2 (not_2_out, S1);
  not not_3 (not_3_out, S2);
  and and_1 (and_1_out, not_1_out, not_2_out, not_3_out, D0);
  and and_2 (and_2_out, not_1_out, not_2_out, S2, D1);
  and and_3 (and_3_out, not_1_out, S1, not_3_out, D2);
  and and_4 (and_4_out, not_1_out, S1, S2, D3);
  and and_5 (and_5_out, S0, not_2_out, not_3_out, D4);
  and and_6 (and_6_out, S0, not_2_out, S2, D5);
  and and_7 (and_7_out, S0, S1, not_3_out, D6);
  and and_8 (and_8_out, S0, S1, S2, D7);
  or or_1 (out_12, and_1_out, and_2_out, and_3_out, and_4_out, and_5_out, and_6_out, and_7_out, and_8_out);
endmodule

module Super_8_Bits_Mux (
  input  [2:0] in_1,
  input  [7:0] B,
  input  [7:0] G,
  input  [7:0] C,
  input  [7:0] E,
  input  [7:0] A,
  input  [7:0] D,
  input  [7:0] F,
  input  [7:0] H,
  output [7:0] out_10
);

  Mux_8bit mux_8bit_1 (
    .D0(A[0]), .D1(B[0]), .D2(C[0]), .D3(D[0]), .D4(E[0]), .D5(F[0]), .D6(G[0]), .D7(H[0]),
    .out_12(out_10[0]), .S0(in_1[2]), .S1(in_1[1]), .S2(in_1[0]));
  Mux_8bit mux_8bit_2 (
    .D0(A[1]), .D1(B[1]), .D2(C[1]), .D3(D[1]), .D4(E[1]), .D5(F[1]), .D6(G[1]), .D7(H[1]),
    .out_12(out_10[1]), .S0(in_1[2]), .S1(in_1[1]), .S2(in_1[0]));
  Mux_8bit mux_8bit_3 (
    .D0(A[2]), .D1(B[2]), .D2(C[2]), .D3(D[2]), .D4(E[2]), .D5(F[2]), .D6(G[2]), .D7(H[2]),
    .out_12(out_10[2]), .S0(in_1[2]), .S1(in_1[1]), .S2(in_1[0]));
  Mux_8bit mux_8bit_4 (
    .D0(A[3]), .D1(B[3]), .D2(C[3]), .D3(D[3]), .D4(E[3]), .D5(F[3]), .D6(G[3]), .D7(H[3]),
    .out_12(out_10[3]), .S0(in_1[2]), .S1(in_1[1]), .S2(in_1[0]));
  Mux_8bit mux_8bit_5 (
    .D0(A[4]), .D1(B[4]), .D2(C[4]), .D3(D[4]), .D4(E[4]), .D5(F[4]), .D6(G[4]), .D7(H[4]),
    .out_12(out_10[4]), .S0(in_1[2]), .S1(in_1[1]), .S2(in_1[0]));
  Mux_8bit mux_8bit_6 (
    .D0(A[5]), .D1(B[5]), .D2(C[5]), .D3(D[5]), .D4(E[5]), .D5(F[5]), .D6(G[5]), .D7(H[5]),
    .out_12(out_10[5]), .S0(in_1[2]), .S1(in_1[1]), .S2(in_1[0]));
  Mux_8bit mux_8bit_7 (
    .D0(A[6]), .D1(B[6]), .D2(C[6]), .D3(D[6]), .D4(E[6]), .D5(F[6]), .D6(G[6]), .D7(H[6]),
    .out_12(out_10[6]), .S0(in_1[2]), .S1(in_1[1]), .S2(in_1[0]));
  Mux_8bit mux_8bit_8 (
    .D0(A[7]), .D1(B[7]), .D2(C[7]), .D3(D[7]), .D4(E[7]), .D5(F[7]), .D6(G[7]), .D7(H[7]),
    .out_12(out_10[7]), .S0(in_1[2]), .S1(in_1[1]), .S2(in_1[0]));

  // Other names for the same wires on the sheet: cc0 = C[0]; cc1 = C[1]; cc2 = C[2]; cc3 = C[3]; cc4 = C[4];
  //   cc5 = C[5]; cc6 = C[6]; cc7 = C[7]; sss = in_1[0]; ss = in_1[1]; s = in_1[2]; c0 = out_10[0]; c1 = out_10[1];
  //   c2 = out_10[2]; c3 = out_10[3]; c4 = out_10[4]; c5 = out_10[5]; c6 = out_10[6]; c7 = out_10[7]
endmodule

module _8_Bits_Not (
  input  [7:0] in_1,
  output [7:0] out_2
);

  assign out_2 = ~in_1;  // NOT_Gate not_1, 8 bits wide
endmodule

module _8_Bits_Or (
  input  [7:0] in_1,
  input  [7:0] in_2,
  output [7:0] out_3
);

  assign out_3 = in_1 | in_2;  // OR_Gate or_1, 8 bits wide
endmodule

module _8_Bits_And (
  input  [7:0] in_1,
  input  [7:0] in_2,
  output [7:0] out_3
);

  assign out_3 = in_1 & in_2;  // AND_Gate and_1, 8 bits wide
endmodule

module EX_Or_8bits (
  input  [7:0] in_1,
  input  [7:0] in_2,
  output [7:0] out_3
);

  assign out_3 = in_1 ^ in_2;  // XOR_Gate xor_1, 8 bits wide
endmodule

module AiAlu (
  input  [7:0] A,
  input  [7:0] B,
  input  Cin,
  input  in_4,
  input  [2:0] in_5,
  output [7:0] out_6,
  output Overflow,
  output out_8
);

  wire [7:0] ex_or_8bits_1_out_3, n8_bits_and_1_out_3, n8_bits_not_1_out_2, n8_bits_not_2_out_2,
       n8_bits_or_1_out_3, sommatore_8_1_out_4, sottrattore_8_1_out_3, super_8_bits_mux_1_out_10;

  _8_Bits_And u_8_bits_and_1 (.in_1(A), .in_2(B), .out_3(n8_bits_and_1_out_3));
  _8_Bits_Or u_8_bits_or_1 (.in_1(A), .in_2(B), .out_3(n8_bits_or_1_out_3));
  EX_Or_8bits ex_or_8bits_1 (.in_1(A), .in_2(B), .out_3(ex_or_8bits_1_out_3));
  _8_Bits_Not u_8_bits_not_1 (.in_1(A), .out_2(n8_bits_not_1_out_2));
  _8_Bits_Not u_8_bits_not_2 (.in_1(B), .out_2(n8_bits_not_2_out_2));
  sommatore_8 sommatore_8_1 (.out_4(sommatore_8_1_out_4), .overflow(Overflow), .A(A), .B(B), .in_3(Cin));
  sottrattore_8 sottrattore_8_1 (.out_3(sottrattore_8_1_out_3), .A(A), .B(B), .Overflow(out_8));
  Super_8_Bits_Mux super_8_bits_mux_1 (
    .B(sottrattore_8_1_out_3), .G(n8_bits_not_2_out_2), .C(n8_bits_and_1_out_3), .E(ex_or_8bits_1_out_3),
    .A(sommatore_8_1_out_4), .D(n8_bits_or_1_out_3), .F(n8_bits_not_1_out_2), .H({8{1'b0}}),
    .out_10(super_8_bits_mux_1_out_10), .in_1(in_5));
  assign out_6 = {8{in_4}} & super_8_bits_mux_1_out_10;  // AND_Gate and_1, 8 bits wide
endmodule

module LaFine (
  input  [7:0] A,
  input  in_2,
  input  [7:0] B,
  input  [2:0] in_4,
  input  in_5,
  output [7:0] out_6,
  output out_7,
  output out_8
);

  AiAlu aialu_1 (.out_6(out_6), .Overflow(out_7), .A(A), .B(B), .Cin(in_2), .in_5(in_4), .out_8(out_8), .in_4(in_5));
endmodule
